# Fritzing sketch HW5_1 (saved by Fritzing 0.9.3b)
breadboards: 1

parts:
  Part1 = Intel Edison Arduinobreakout
  S1 = Pushbutton [package="[THT]"]
  LED1 = LED - 5mm [color="Red (633nm)" package="5 mm [THT]"]
  R1 = Resistor [tolerance=±5% resistance=220 package=THT]
  T1 = LM35 Temperature Sensor [package="TO92 [THT]"]
  R2 = Resistor [tolerance=±5% resistance=220 package="2010 [SMD]"]
  S2 = Momentary Switch [package=ksa_sealed_tac_switch]
  LED2 = smd LED [color="Red (633nm)" package="0805 [SMD]"]

nets:
  N1: Part1.A0, T1.Vout
  N2: Part1.D8, Part1.D7, R2.Pin_0
  N3: Part1.D13/SCK, Part1.D2, R1.Pin_0
  GND: Part1.GND, LED1.cathode, T1.GND, LED2.cathode
  N4: Part1.5V, S1.Pin_1, S1.Pin_2, S1.Pin_3, S1.Pin_4, T1.+Vs, S2.1, S2.3
  N5: LED1.anode, R1.Pin_1
  N6: R2.Pin_1, LED2.anode
  N7: S2.2, S2.4
